# Fritzing sketch schematics (saved by Fritzing 0.9.3b)
breadboards: 1

parts:
  Part1 = Arduino Uno (Rev3)
  Part2 = 10-DOF IMU L3GD20H + LSM303 + BMP180 [part_number=1604]
  J0 = Basic Servo
  J1 = Basic Servo
  J2 = Basic Servo
  J3 = Basic Servo
  J4 = Basic Servo
  J5 = Basic Servo
  J6 = Basic Servo
  U1 = FS1000A - 433Mhz RF Transmitter [package=THT]
  U2 = XD-RF-5V [package=THT]  # not connected
  GY-NEO6MV3 = SUP500F [package=sup500f]
  JP2 = Header 3 [package=jst-3-smd]
  JP4 = Header 1 [package=luxeon-pad]
  JP5 = Header 1 [package=luxeon-pad]
  BAT1 = BC9VPC [package=bc9vpc]
  D1 = Diode [package=diode-1n4148]
  R3 = Resistor [tolerance=±5% resistance=1k package="1206 [SMD]"]
  R4 = Resistor [tolerance=±5% resistance=1.5k package="1206 [SMD]"]
  LED1 = smd LED [color="Red (633nm)" package="1206 [SMD]"]
  R5 = Resistor [tolerance=±5% resistance=330 package="1206 [SMD]"]

nets:
  N1: Part1.A1, R3.Pin_0, R4.Pin_1
  N2: Part1.A2, GY-NEO6MV3.RX-I
  N3: Part1.A3, GY-NEO6MV3.TX-O
  N4: Part1.A5/SCL, Part2.SCL
  N5: Part1.D8, J2.pulse
  N6: Part1.D9_PWM, U1.DATA
  N7: Part1.D10_PWM/SS, J1.pulse
  N8: Part1.D11_PWM/MOSI, J0.pulse
  N9: Part1.D12/MISO, J5.pulse
  N10: Part1.D13/SCK, J6.pulse
  N11: Part1.A4/SDA, Part2.SDA
  N12: Part1.D0/RX, LED1.anode
  N13: Part1.D1/TX, JP4.1
  N14: Part1.D2, JP2.1
  N15: Part1.D3_PWM, JP2.2
  N16: Part1.D4, JP2.3
  N17: Part1.D5_PWM, JP5.1
  N18: Part1.D6_PWM, J4.pulse
  N19: Part1.D7, J3.pulse
  5V: Part1.5V, Part2.VIN, GY-NEO6MV3.VCC
  GND: Part1.GND, Part2.GND, J5.gnd, J6.gnd, GY-NEO6MV3.GND, BAT1.V-, R3.Pin_1, R5.Pin_1
  VCC: Part1.VIN, J0.vcc, J1.vcc, J2.vcc, J3.vcc, J4.vcc, J5.vcc, J6.vcc, U1.VCC, D1.C, R4.Pin_0
  GND_2: J0.gnd, J1.gnd, J2.gnd, J3.gnd, J4.gnd, U1.GND
  N20: BAT1.V+, D1.A
  N21: LED1.cathode, R5.Pin_0

notes:
  4 Surface control motor 1Motor control
  (J0 -J4)
  2 Droping servo controls
  J6-J5
  Transmitter
  Reciever (to be connected to ground station
  GPS
  5 channel reciever ouputs

custom parts:
  10-DOF IMU L3GD20H + LSM303 + BMP180: This inertial-measurement-unit combines 3 of the best quality sensors available on the market to give you 11 axes of data: 3 axes of accelerometer data, 3 axes gyroscopic, 3 axes magnetic (compass), barometric pressure/altitude and temperature. We tested many different 'combination' sensors and found these were the best value, with stable and reliable readings.
  FS1000A - 433Mhz RF Transmitter: This is 433Mhz RF transmitter with receiver kit for Arduino ARM MCU wireless Application environment: Remote control switch, receiver module, motorcycles, automobile anti-theft products, home security products, electric doors, shutter doors, windows, remote control socket, remote control LED, remote audio remote control electric doors, garage door remote control, remote control retractable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
  XD-RF-5V: This is 433Mhz RF transmitter with receiver kit for Arduino ARM MCU wireless Application environment: Remote control switch, receiver module, motorcycles, automobile anti-theft products, home security products, electric doors, shutter doors, windows, remote control socket, remote control LED, remote audio remote control electric doors, garage door remote control, remote control retractable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
